// Logisim project 6502_computer.circ as structural Verilog: 1 circuit, main circuit main
module main (
);

  wire clock_1_out;
  wire [7:0] w65c02s_pdip_40_1_p13;
  wire [15:0] w65c02s_pdip_40_1_p1;

  Clock clock_1 (.out(clock_1_out));
  // W65C02S__PDIP_40 w65c02s_pdip_40_1: pin names not known; wires that end beside it: w65c02s_pdip_40_1_p1[0], w65c02s_pdip_40_1_p1[1], w65c02s_pdip_40_1_p1[2], w65c02s_pdip_40_1_p1[3], w65c02s_pdip_40_1_p1[4], w65c02s_pdip_40_1_p1[5], w65c02s_pdip_40_1_p1[6], w65c02s_pdip_40_1_p1[7], w65c02s_pdip_40_1_p1[8], w65c02s_pdip_40_1_p1[9], w65c02s_pdip_40_1_p1[10], w65c02s_pdip_40_1_p1[11], w65c02s_pdip_40_1_p13[0], w65c02s_pdip_40_1_p13[1], w65c02s_pdip_40_1_p13[2], w65c02s_pdip_40_1_p13[3], w65c02s_pdip_40_1_p13[4], w65c02s_pdip_40_1_p13[5], w65c02s_pdip_40_1_p13[6], w65c02s_pdip_40_1_p13[7], w65c02s_pdip_40_1_p1[15], w65c02s_pdip_40_1_p1[14], w65c02s_pdip_40_1_p1[13], w65c02s_pdip_40_1_p1[12]
  RAM ram_1 (.addr(w65c02s_pdip_40_1_p1[7:0]), .data(w65c02s_pdip_40_1_p13));  // open: sel, clk, ld, clr
  ROM rom_1 (.addr(w65c02s_pdip_40_1_p1[7:0]), .data(w65c02s_pdip_40_1_p13));  // open: sel
  // Pins of 8 and 16 bits meet at w65c02s_pdip_40_1_p1
endmodule
